// Logisim project dir_test.circ as structural Verilog: 1 circuit, main circuit main
module main (
);

  wire button_1_out, button_2_out, clock_1_out, counter_1_p1, counter_3_carry, counter_4_carry,
       counter_7_carry, counter_8_carry;
  wire [3:0] binary_to_bcd_1_p1, binary_to_bcd_1_p2, counter_1_p3, counter_1_p4, counter_1_p5;
  wire [7:0] counter_2_q, counter_5_q, counter_6_q, counter_8_q, counter_9_q;

  Hex_Digit_Display hex_digit_display_1 (.value(counter_1_p3));  // open: dp
  Clock clock_1 (.out(clock_1_out));
  Button button_1 (.out(button_1_out));
  Button button_2 (.out(button_2_out));
  Hex_Digit_Display hex_digit_display_2 (.value(counter_1_p5));  // open: dp
  Hex_Digit_Display hex_digit_display_3 (.value(counter_1_p4));  // open: dp
  // Binary_to_BCD binary_to_bcd_1: pin names not known; wires that end beside it: binary_to_bcd_1_p1, binary_to_bcd_1_p2
  // Counter #(.width(16), .max('hffff)) counter_1: pin names not known; wires that end beside it: counter_1_p1, button_2_out, counter_1_p3, counter_1_p4, counter_1_p5
  or or_1 (counter_1_p1, clock_1_out, button_1_out);
  Hex_Digit_Display hex_digit_display_4 (.value(binary_to_bcd_1_p2));  // open: dp
  Hex_Digit_Display hex_digit_display_5 (.value(binary_to_bcd_1_p1));  // open: dp
  Counter counter_2 (.Q(counter_2_q), .clk(counter_3_carry), .clr(button_2_out));  // open: load, D, count, carry
  Counter #(.width(3), .max('h7)) counter_3 (
    .carry(counter_3_carry), .clk(counter_1_p1), .clr(button_2_out));  // open: load, D, count, Q
  Counter #(.width(4), .max('hf)) counter_4 (
    .carry(counter_4_carry), .clk(counter_1_p1), .clr(button_2_out));  // open: load, D, count, Q
  Counter counter_5 (.Q(counter_5_q), .clk(counter_4_carry), .clr(button_2_out));  // open: load, D, count, carry
  Counter counter_6 (.Q(counter_6_q), .clk(counter_7_carry), .clr(button_2_out));  // open: load, D, count, carry
  Counter #(.width(5), .max('h1f)) counter_7 (
    .carry(counter_7_carry), .clk(counter_1_p1), .clr(button_2_out));  // open: load, D, count, Q
  Counter counter_8 (
    .Q(counter_8_q), .carry(counter_8_carry), .clk(counter_1_p1), .clr(button_2_out));  // open: load, D, count
  Counter counter_9 (.Q(counter_9_q), .clk(counter_8_carry), .clr(button_2_out));  // open: load, D, count, carry
  // Color_Screen color_screen_1: pin names not known; wires that end beside it: counter_8_q, counter_9_q, counter_6_q, counter_5_q, counter_2_q, counter_1_p1
endmodule
