// Logisim project testing.circ as structural Verilog: 1 circuit, main circuit main
module main (
);

  wire button_1_out, clock_1_out, counter_1_carry, counter_2_carry, t_ff_1_q, t_ff_1_qn;
  wire [7:0] counter_1_q, counter_2_q, multiplier_1_out, random_1_out, random_2_out;

  Random random_1 (.clk(clock_1_out), .out(random_1_out));  // open: next, clr
  Multiplier multiplier_1 (.a(random_1_out), .b(random_2_out), .out(multiplier_1_out));  // open: cin, cout
  Random random_2 (.clk(clock_1_out), .out(random_2_out));  // open: next, clr
  Clock clock_1 (.out(clock_1_out));
  Counter counter_1 (
    .Q(counter_1_q), .carry(counter_1_carry), .clk(clock_1_out), .clr(button_1_out));  // open: load, D, count
  Counter counter_2 (
    .Q(counter_2_q), .carry(counter_2_carry), .clk(counter_1_carry), .clr(button_1_out));  // open: load, D, count
  T_Flip_Flop t_ff_1 (
    .clk(counter_2_carry), .T(counter_2_carry), .Q(t_ff_1_q), .Qn(t_ff_1_qn), .preset(button_1_out));  // open: reset, en
  Button button_1 (.out(button_1_out));
  // Screen screen_1: pin names not known; wires that end beside it: button_1_out, counter_2_q, counter_1_q, counter_1_q, counter_2_q, t_ff_1_q, t_ff_1_qn, button_1_out
  // Color_Screen color_screen_1: pin names not known; wires that end beside it: counter_2_q, counter_1_q, counter_1_q, counter_2_q, random_1_out, multiplier_1_out, random_2_out, clock_1_out, button_1_out
endmodule
