// Logisim project testing.circ as structural Verilog: 1 circuit, main circuit main
module main (
);

  wire button_2_out, clock_1_out;
  wire [7:0] color_screen_1_p3, color_screen_1_p4, color_screen_1_p5, counter_1_q, counter_1_q_2,
       random_1_out;

  // Toggle_button toggle_button_1: pin names not known
  Button button_1 ();  // open: out
  Button button_2 (.out(button_2_out));
  Clock clock_1 (.out(clock_1_out));
  Random random_1 (.clk(clock_1_out), .out(random_1_out));  // open: next, clr
  Counter #(.width(16), .max('hffff)) counter_1 (
    .Q({counter_1_q_2, counter_1_q}), .clk(clock_1_out), .clr(button_2_out));  // open: load, D, count, carry
  // Color_Screen color_screen_1: pin names not known; wires that end beside it: counter_1_q, counter_1_q_2, color_screen_1_p3, color_screen_1_p4, color_screen_1_p5, clock_1_out, button_2_out
  Multiplier multiplier_1 (
    .a(random_1_out), .b(counter_1_q_2), .out(color_screen_1_p4), .cout(color_screen_1_p3));  // open: cin
  Adder adder_1 (.a(random_1_out), .b(counter_1_q_2), .out(color_screen_1_p5));  // open: cin, cout
endmodule
